# Fritzing sketch wiring (saved by Fritzing 0.9.3b)

parts:
  WeMos_D1_Mini1 = WeMos D1 Mini
  Part1 = Matrix LED de 8x8 basada en MAX7219

nets:
  5V: WeMos_D1_Mini1.5V, Part1.VCC
  N1: WeMos_D1_Mini1.D5, Part1.CLK
  N2: WeMos_D1_Mini1.D7, Part1.DIN
  N3: WeMos_D1_Mini1.D8, Part1.CS
  N4: WeMos_D1_Mini1.G, Part1.GND

notes:
  CATATAN :
  Urutan pin modul matrix led tidak selalu sama, silakan disesuaikan
  VCC, GND, DIN, CLK ,CS
  VCC, GND, DIN, CS, CLK
